// Logisim project Practical 1.circ as structural Verilog: 1 circuit, main circuit main
module main (
  input  [3:0] in_1,
  input  [3:0] in_2,
  input  [3:0] in_3,
  input  [3:0] in_4,
  input  in_5,
  input  [1:0] in_6,
  input  [1:0] in_7,
  input  in_8
);

  wire clock_1_out, clock_2_out, decoder_1_out0, decoder_1_out1, decoder_1_out2, decoder_1_out3;
  wire [3:0] B_q, C_q, D_q, multiplexer_1_out, register_1_q;

  Clock clock_1 (.out(clock_1_out));
  Register #(.width(4)) register_1 (.D(in_1), .Q(register_1_q), .clk(clock_1_out));  // open: en, clr
  Multiplexer #(.select(2)) multiplexer_1 (
    .in0(register_1_q[0]), .in1(B_q[0]), .in2(C_q[0]), .in3(D_q[0]), .out(multiplexer_1_out[0]), .sel(in_7),
    .en(in_8));
  Register #(.width(4)) B (.D(in_2), .Q(B_q), .clk(clock_1_out));  // open: en, clr
  Multiplexer #(.select(2)) multiplexer_2 (
    .in0(register_1_q[1]), .in1(B_q[1]), .in2(C_q[1]), .in3(D_q[1]), .out(multiplexer_1_out[1]), .sel(in_7),
    .en(in_8));
  Register #(.width(4)) C (.D(in_3), .Q(C_q), .clk(clock_1_out));  // open: en, clr
  Multiplexer #(.select(2)) multiplexer_3 (
    .in0(register_1_q[2]), .in1(B_q[2]), .in2(C_q[2]), .in3(D_q[2]), .out(multiplexer_1_out[2]), .sel(in_7),
    .en(in_8));
  Register #(.width(4)) D (.D(in_4), .Q(D_q), .clk(clock_1_out));  // open: en, clr
  Multiplexer #(.select(2)) multiplexer_4 (
    .in0(register_1_q[3]), .in1(B_q[3]), .in2(C_q[3]), .in3(D_q[3]), .out(multiplexer_1_out[3]), .sel(in_7),
    .en(in_8));
  Clock clock_2 (.out(clock_2_out));
  Register #(.width(4)) register_2 (.D(multiplexer_1_out), .en(decoder_1_out0), .clk(clock_2_out));  // open: Q, clr
  Register #(.width(4)) register_3 (.D(multiplexer_1_out), .en(decoder_1_out1), .clk(clock_2_out));  // open: Q, clr
  Register #(.width(4)) register_4 (.D(multiplexer_1_out), .en(decoder_1_out2), .clk(clock_2_out));  // open: Q, clr
  Register #(.width(4)) register_5 (.D(multiplexer_1_out), .en(decoder_1_out3), .clk(clock_2_out));  // open: Q, clr
  Decoder #(.select(2)) decoder_1 (
    .out0(decoder_1_out0), .out1(decoder_1_out1), .out2(decoder_1_out2), .out3(decoder_1_out3), .sel(in_6),
    .en(in_5));

  // Notes on the sheet:
  //   CHAMPAWAT NAGENDRASINGH INDRASINGH 240283107002
endmodule
